# Fritzing sketch Hypnos (saved by Fritzing 0.9.2b)

parts:
  Composant1 = Arduino Nano (Rev3.0) (ICSP)
  ZS-042_RTC1 = ZS-042 RTC Module
  8x8_LED_matrix_MAX1 = 8x8 Red 8x8 LED Matrix with MAX7219

nets:
  GND: Composant1.GND, ZS-042_RTC1.GND, 8x8_LED_matrix_MAX1.GND
  N1: Composant1.D10, 8x8_LED_matrix_MAX1.CS
  N2: Composant1.D11/MOSI, 8x8_LED_matrix_MAX1.GND_PT, 8x8_LED_matrix_MAX1.CLK
  N3: Composant1.D12/MISO, 8x8_LED_matrix_MAX1.DIN
  5V: Composant1.5V, 8x8_LED_matrix_MAX1.VCC
  N4: Composant1.A5, ZS-042_RTC1.SCL
  N5: Composant1.A4, ZS-042_RTC1.SDA
  3V3: Composant1.3V3, ZS-042_RTC1.VCC

custom parts:
  8x8 Red 8x8 LED Matrix with MAX7219: Description: 8 by 8 red LED matrix with a MAX7219 controller.
